// Digital circuit familiarizacao_verilog_85.dig as structural Verilog
module familiarizacao_verilog_85 (
  input  [3:0] A,
  input  [3:0] B,
  input  ALBi,
  input  AGBi,
  input  AEBi,
  output AGBo,
  output AEBo,
  output ALBo
);

  comparador_85 #(.applicationType("IVERILOG")) u_comparador_85 (
    .A(A), .B(B), .ALBi(ALBi), .AGBi(AGBi), .AEBi(AEBi), .ALBo(ALBo), .AGBo(AGBo), .AEBo(AEBo));
endmodule

/* Code of comparador_85:
module comparador_85 (ALBi, AGBi, AEBi, A, B, ALBo, AGBo, AEBo);

    input[3:0] A, B;
    input      ALBi, AGBi, AEBi;
    output     ALBo, AGBo, AEBo;
    wire[4:0]  CSL, CSG;

    assign CSL  = ~A + B + ALBi;
    assign ALBo = ~CSL[4];
    assign CSG  = A + ~B + AGBi;
    assign AGBo = ~CSG[4];
    assign AEBo = ((A == B) && AEBi);

endmodule /* comparador_85 * /
*/
