// Digital circuit circuito_exp4_desafio.dig as structural Verilog
module circuito_exp4_desafio (
  input  in_1,
  input  in_2,
  input  [3:0] in_9,
  output out_3,
  output out_4,
  output out_5,
  output out_6,
  output out_7,
  output out_8,
  output out_10,
  output out_11,
  output out_12,
  output out_13
);

  wire button_1_out;
  wire [3:0] u_circuito_exp4_desafio_db_chaves, u_circuito_exp4_desafio_db_contagem,
       u_circuito_exp4_desafio_db_estado, u_circuito_exp4_desafio_db_memoria;

  Button button_1 (.out(button_1_out));
  circuito_exp4_desafio #(.applicationType("IVERILOG")) u_circuito_exp4_desafio (
    .clock(button_1_out), .reset(in_1), .iniciar(in_2), .chaves(in_9), .pronto(out_3), .acertou(out_4),
    .errou(out_5), .db_igual(out_6), .db_iniciar(out_7), .db_zeraC(out_8), .db_contaC(out_10),
    .db_fimC(out_11), .db_zeraR(out_12), .db_registraR(out_13),
    .db_contagem(u_circuito_exp4_desafio_db_contagem), .db_memoria(u_circuito_exp4_desafio_db_memoria),
    .db_chaves(u_circuito_exp4_desafio_db_chaves), .db_estado(u_circuito_exp4_desafio_db_estado));
  Seven_Seg_Hex seven_seg_hex_1 (.d(u_circuito_exp4_desafio_db_contagem), .dp(1'b0));
  Seven_Seg_Hex seven_seg_hex_2 (.d(u_circuito_exp4_desafio_db_memoria), .dp(1'b0));
  Seven_Seg_Hex seven_seg_hex_3 (.d(u_circuito_exp4_desafio_db_chaves), .dp(1'b0));
  Seven_Seg_Hex seven_seg_hex_4 (.d(u_circuito_exp4_desafio_db_estado), .dp(1'b0));
endmodule

/* Code of circuito_exp4_desafio:
module circuito_exp4_desafio (
    input        clock,
    input        reset,
    input        iniciar,
    input  [3:0] chaves,
    output       pronto,

    output       acertou,
    output       errou,

    output       db_igual,
    output       db_iniciar,
    output       db_zeraC,
    output       db_contaC,
    output       db_fimC,
    output       db_zeraR,
    output       db_registraR,
    output [3:0] db_contagem,
    output [3:0] db_memoria,
    output [3:0] db_chaves,
    output [3:0] db_estado
);

wire [3:0] s_chaves;
wire [3:0] s_contagem;
wire [3:0] s_memoria;
wire [3:0] s_estado;
wire wireFimC;
wire wireIniciar;
wire wireContaC;
wire wireZeraC;
wire wireZeraR;
wire wireRegistraR;
wire wireIgual;

assign db_iniciar = wireIniciar;
assign wireIniciar = iniciar;
assign db_zeraC = wireZeraC;
assign db_contaC = wireContaC;
assign db_fimC = wireFimC;
assign db_zeraR = wireZeraR;
assign db_registraR = wireRegistraR;
assign db_igual = wireIgual;
assign db_contagem = s_contagem;

exp4_fluxo_dados fluxo (
    .clock ( clock ),
    .chaves ( chaves ),
    .zeraR ( wireZeraR ),
    .registraR ( wireRegistraR ),
    .contaC ( wireContaC ),
    .zeraC ( wireZeraC ),
    .chavesIgualMemoria ( wireIgual ),
    .fimC ( wireFimC ),
    .db_contagem ( s_contagem ),
    .db_chaves ( s_chaves ),
    .db_memoria ( s_memoria )
);

exp4_unidade_controle uc (
    .clock ( clock ),
    .reset ( reset ),
    .iniciar ( wireIniciar ),
    .fimC ( wireFimC ),
    .igual ( wireIgual ),
    .zeraC ( wireZeraC ),
    .contaC ( wireContaC ),
    .zeraR ( wireZeraR ),
    .registraR ( wireRegistraR ),
    .pronto ( pronto ),
    .db_estado ( s_estado ),
    .acertou ( acertou ),
    .errou ( errou )
);

hexa7seg HEX2 (
    .hexa ( s_chaves ),
    .display ( db_chaves )
);

hexa7seg HEX0 (
    .hexa ( s_contagem ),
    .display ( db_contagem )
);

hexa7seg HEX1 (
    .hexa ( s_memoria ),
    .display ( db_memoria )
);

hexa7seg HEX5 (
    .hexa ( s_estado ),
    .display ( db_estado )
);


endmodule

module comparador_85 (ALBi, AGBi, AEBi, A, B, ALBo, AGBo, AEBo);

    input[3:0] A, B;
    input      ALBi, AGBi, AEBi;
    output     ALBo, AGBo, AEBo;
    wire[4:0]  CSL, CSG;

    assign CSL  = ~A + B + ALBi;
    assign ALBo = ~CSL[4];
    assign CSG  = A + ~B + AGBi;
    assign AGBo = ~CSG[4];
    assign AEBo = ((A == B) && AEBi);

endmodule

module contador_163 ( clock, clr, ld, ent, enp, D, Q, rco );
    input clock, clr, ld, ent, enp;
    input [3:0] D;
    output reg [3:0] Q;
    output reg rco;

	 initial begin
		Q = 4'd0;
    end
	 
    always @ (posedge clock)
        if (~clr)               Q <= 4'd0;
        else if (~ld)           Q <= D;
        else if (ent && enp)    Q <= Q + 1;
        else                    Q <= Q;
 
    always @ (Q or ent)
        if (ent && (Q == 4'd15))   rco = 1;
        else                       rco = 0;
endmodule

module exp4_fluxo_dados (
                        input        clock,
                        input  [3:0] chaves,
                        input        zeraR,
                        input        registraR,
                        input        contaC,
                        input        zeraC,

                        output       chavesIgualMemoria,
                        output       fimC,
                        output [3:0] db_contagem,
                        output [3:0] db_chaves, 
                        output [3:0] db_memoria
);
    
    wire ALBo, AGBo;
    wire [3:0] s_endereco;  // sinal interno para interligacao dos componentes
    wire [3:0] s_chaves;
    wire [3:0] s_dado;

    assign db_contagem = s_endereco;
    assign db_chaves = s_chaves;
    assign db_memoria = s_dado;

    // contador_163
    contador_163 contador (
      .clock( clock ),
      .clr  ( ~zeraC ),
      .ld   ( 1'b1 ),
      .ent  ( 1'b1 ),
      .enp  ( contaC ),
      .D    ( 4'b0000 ),
      .Q    ( s_endereco ),
      .rco  ( fimC )
    );

     sync_rom_16x4 mem (
      .clock   ( clock ),
      .address ( s_endereco ),
      .data_out( s_dado )
     );

     registrador_4 reg1 (
      .clock ( clock ),
      .clear ( zeraR ),
      .enable( registraR ),
      .D     ( chaves ),
      .Q     ( s_chaves )
     );

    // comparador_85
    comparador_85 comparador (
      .A   ( s_dado ),
      .B   ( s_chaves ),
      .ALBi( 1'b0 ),
      .AGBi( 1'b0 ),
      .AEBi( 1'b1 ),
      .ALBo( ALBo ),
      .AGBo( AGBo ),
      .AEBo( chavesIgualMemoria )
    );

 endmodule

module exp4_unidade_controle (
    input      clock,
    input      reset,
    input      iniciar,
    input      fimC,

    input      igual,

    output reg zeraC,
    output reg contaC,
    output reg zeraR,
    output reg registraR,
    output reg pronto,
    output reg [3:0] db_estado,
    output reg acertou,
    output reg errou
);

    // Define estados
    parameter inicial    = 4'b0000;  // 0
    parameter preparacao = 4'b0001;  // 1
    parameter registra   = 4'b0100;  // 4
    parameter comparacao = 4'b0101;  // 5
    parameter proximo    = 4'b0110;  // 6
    parameter fim        = 4'b1100;  // C
	 parameter errouState = 4'b1101;  // D

    // Variaveis de estado
    reg [3:0] Eatual, Eprox;

    // Memoria de estado
    always @(posedge clock or posedge reset) begin
        if (reset)
            Eatual <= inicial;
        else
            Eatual <= Eprox;
    end

    // Logica de proximo estado
    always @* begin
        case (Eatual)
            inicial:     Eprox = iniciar ? preparacao : inicial;
            preparacao:  Eprox = registra;
            registra:    Eprox = comparacao;
            comparacao:  Eprox = fimC ? fim : ~igual ? errouState : proximo; //
            proximo:     Eprox = registra;
            fim:         Eprox = inicial;
				errouState:  Eprox = inicial;
            default:     Eprox = inicial;
        endcase
    end

    // Logica de saida (maquina Moore)
    always @* begin
        zeraC     = (Eatual == inicial || Eatual == preparacao) ? 1'b1 : 1'b0;
        zeraR     = (Eatual == inicial || Eatual == preparacao) ? 1'b1 : 1'b0;
        registraR = (Eatual == registra) ? 1'b1 : 1'b0;
        contaC    = (Eatual == proximo) ? 1'b1 : 1'b0;
        pronto    = (Eatual == fim || Eatual == errouState) ? 1'b1 : 1'b0; 
        acertou   = (Eatual == fim) ? 1'b1 : 1'b0; 
        errou     = (Eatual == errouState) ? 1'b1 : 1'b0;               
                                                      

        // Saida de depuracao (estado)
        case (Eatual)
            inicial:     db_estado = 4'b0000;  // 0
            preparacao:  db_estado = 4'b0001;  // 1
            registra:    db_estado = 4'b0100;  // 4
            comparacao:  db_estado = 4'b0101;  // 5
            proximo:     db_estado = 4'b0110;  // 6
            fim:         db_estado = 4'b1100;  // C
            default:     db_estado = 4'b1111;  // F
        endcase
    end

endmodule

module hexa7seg (hexa, display);
    input      [3:0] hexa;
    output reg [3:0] display;

    /*
     *    ---
     *   | 0 |
     * 5 |   | 1
     *   |   |
     *    ---
     *   | 6 |
     * 4 |   | 2
     *   |   |
     *    ---
     *     3
     * /
        
    always @(hexa)
    case (hexa)
        4'h0:    display = 4'h0;
        4'h1:    display = 4'h1;
        4'h2:    display = 4'h2;
        4'h3:    display = 4'h3;
        4'h4:    display = 4'h4;
        4'h5:    display = 4'h5;
        4'h6:    display = 4'h6;
        4'h7:    display = 4'h7;
        4'h8:    display = 4'h8;
        4'h9:    display = 4'h9;
        4'ha:    display = 4'ha;
        4'hb:    display = 4'hb;
        4'hc:    display = 4'hc;
        4'hd:    display = 4'hd;
        4'he:    display = 4'he;
        4'hf:    display = 4'hf;
        default: display = 4'h0;
    endcase
endmodule

module registrador_4 (
    input        clock,
    input        clear,
    input        enable,
    input  [3:0] D,
    output [3:0] Q
);

    reg [3:0] IQ;

    always @(posedge clock or posedge clear) begin
        if (clear)
            IQ <= 0;
        else if (enable)
            IQ <= D;
    end

    assign Q = IQ;

endmodule

module sync_rom_16x4 (clock, address, data_out);
    input            clock;
    input      [3:0] address;
    output reg [3:0] data_out;

    always @ (posedge clock)
    begin
        case (address)
            4'b0000: data_out = 4'b0001;
            4'b0001: data_out = 4'b0010;
            4'b0010: data_out = 4'b0100;
            4'b0011: data_out = 4'b1000;
            4'b0100: data_out = 4'b0100;
            4'b0101: data_out = 4'b0010;
            4'b0110: data_out = 4'b0001;
            4'b0111: data_out = 4'b0001;
            4'b1000: data_out = 4'b0010;
            4'b1001: data_out = 4'b0010;
            4'b1010: data_out = 4'b0100;
            4'b1011: data_out = 4'b0100;
            4'b1100: data_out = 4'b1000;
            4'b1101: data_out = 4'b1000;
            4'b1110: data_out = 4'b0001;
            4'b1111: data_out = 4'b0100;
        endcase
    end
endmodule
*/
